// Logisim project SinalDeTransito.circ as structural Verilog: 1 circuit, main circuit main
module main (
);

  wire and_1_out, and_2_out, and_3_out, and_4_out, button_1_out, clock_1_out, j_k_ff_1_q, nor_1_out,
       nor_2_out, or_1_out, or_2_out, undriven;
  wire [4:0] counter_1_q;

  LED led_1 (.in(and_1_out));
  LED led_2 (.in(and_2_out));
  nor nor_1 (nor_1_out, and_1_out, and_2_out);
  LED led_3 (.in(nor_1_out));
  and and_1 (and_1_out, ~counter_1_q[4], ~counter_1_q[3], counter_1_q[2]);  // AND_Gate
  and and_2 (and_2_out, ~counter_1_q[4], ~counter_1_q[3], ~counter_1_q[2], counter_1_q[1], counter_1_q[0]);  // AND_Gate
  Clock clock_1 (.out(clock_1_out));
  Button button_1 (.out(button_1_out));
  Counter #(.width(5), .max('h10)) counter_1 (
    .load(j_k_ff_1_q), .D(5'b00001), .Q(counter_1_q), .clk(clock_1_out), .down(undriven));  // open: count, carry, clr, preset
  or or_1 (or_1_out, counter_1_q[3], counter_1_q[4]);
  and and_3 (and_3_out, or_1_out, button_1_out);
  J_K_Flip_Flop j_k_ff_1 (
    .J(j_k_ff_1_q), .clk(clock_1_out), .K(clock_1_out), .Q(j_k_ff_1_q), .preset(and_3_out));  // open: Qn, reset
  or or_2 (or_2_out, counter_1_q[4], counter_1_q[3], ~counter_1_q[2]);  // OR_Gate
  and and_4 (and_4_out, ~counter_1_q[4], ~counter_1_q[3], counter_1_q[2], counter_1_q[1], counter_1_q[0]);  // AND_Gate
  LED led_4 (.in(or_2_out));
  LED led_5 (.in(and_4_out));
  LED led_6 (.in(nor_2_out));
  nor nor_2 (nor_2_out, or_2_out, and_4_out);

  // Notes on the sheet:
  //   SINAL PARA CARROS
  //   Clock
  //   b
  //   SINAL PARA PEDESTRES
  //   Pare
  //   Atravesse
  //    Vermelho Piscante
endmodule
