// Logisim project Circuito_Lista02.circ as structural Verilog: 1 circuit, main circuit main
module main (
);

  wire and_1_out, and_2_out, and_3_out, and_4_out, or_1_out, or_2_out, or_3_out, or_4_out, undriven,
       undriven_2, undriven_3, undriven_4, undriven_5, undriven_6, undriven_7, undriven_8;

  or or_1 (or_1_out, undriven, undriven_3);
  and and_1 (and_1_out, or_1_out, or_2_out, or_3_out);
  or or_2 (or_2_out, undriven, undriven_6, undriven_8);
  or or_3 (or_3_out, undriven_3, undriven_6, undriven_8);
  and and_2 (and_2_out, undriven_2, undriven_4, undriven_5);
  or or_4 (or_4_out, and_2_out, and_3_out, and_4_out);
  and and_3 (and_3_out, undriven_2, undriven_4, undriven_7);
  and and_4 (and_4_out, undriven_5, undriven_7);

  // Notes on the sheet:
  //   A0
  //   A1
  //   ¬A1
  //   ¬A0
  //   ¬A3
  //   ¬A2
  //   A2
  //   A3
  //   P0
  //   P1
endmodule
