// Logisim project Lista04_NOR_Universal.circ as structural Verilog: 1 circuit, main circuit main
module main (
);

  wire dipswitch_1_p1, dipswitch_2_p1, dipswitch_2_p2, dipswitch_3_p1, dipswitch_3_p2, dipswitch_4_p1,
       dipswitch_4_p2, nor_1_out, nor_2_out, nor_3_out, nor_4_out, nor_5_out, nor_6_out, nor_7_out,
       nor_8_out, nor_9_out, nor_10_out, nor_11_out;

  // DipSwitch #(.NSwitches(1)) dipswitch_1: pin names not known; wires that end beside it: dipswitch_1_p1
  // DipSwitch #(.NSwitches(2)) dipswitch_2: pin names not known; wires that end beside it: dipswitch_2_p1, dipswitch_2_p2
  // DipSwitch #(.NSwitches(2)) dipswitch_3: pin names not known; wires that end beside it: dipswitch_3_p1, dipswitch_3_p2
  // DipSwitch #(.NSwitches(2)) dipswitch_4: pin names not known; wires that end beside it: dipswitch_4_p1, dipswitch_4_p2
  nor nor_1 (nor_1_out, dipswitch_1_p1, dipswitch_1_p1);
  nor nor_2 (nor_2_out, dipswitch_2_p1, dipswitch_2_p1);
  nor nor_3 (nor_3_out, dipswitch_2_p2, dipswitch_2_p2);
  nor nor_4 (nor_4_out, dipswitch_3_p1, dipswitch_3_p2);
  nor nor_5 (nor_5_out, dipswitch_4_p1, dipswitch_4_p2);
  nor nor_6 (nor_6_out, dipswitch_4_p2, dipswitch_4_p2);
  nor nor_7 (nor_7_out, dipswitch_4_p1, dipswitch_4_p1);
  LED led_1 (.in(nor_1_out));
  LED led_2 (.in(nor_8_out));
  nor nor_8 (nor_8_out, nor_2_out, nor_3_out);
  LED led_3 (.in(nor_9_out));
  nor nor_9 (nor_9_out, nor_4_out, nor_4_out);
  LED led_4 (.in(nor_10_out));
  nor nor_10 (nor_10_out, nor_5_out, nor_11_out);
  nor nor_11 (nor_11_out, nor_6_out, nor_7_out);
endmodule
