// Logisim project counter.circ as structural Verilog: 1 circuit, main circuit main
module main (
);

  wire and_1_out, and_2_out, and_3_out, and_4_out, and_5_out, and_6_out, button_1_out, button_2_out,
       demultiplexer_1_out0, demultiplexer_1_out1, demultiplexer_2_out0, demultiplexer_2_out1,
       demultiplexer_3_out0, demultiplexer_3_out1, demultiplexer_4_out0, demultiplexer_4_out1,
       demultiplexer_5_out0, demultiplexer_5_out1, or_1_out, or_2_out, or_3_out, or_4_out, or_5_out,
       t_ff_2_q, undriven, undriven_2, undriven_3, undriven_4, undriven_5, xnor_1_out, xnor_2_out,
       xnor_3_out, xnor_4_out;
  wire [3:0] slider_1_out, slider_2_out, t_ff_5_q;

  and and_1 (and_1_out, xnor_1_out, xnor_2_out, xnor_3_out, xnor_4_out);
  or or_1 (or_1_out, and_1_out, button_2_out);
  T_Flip_Flop t_ff_1 (
    .clk(button_1_out), .T(and_2_out), .Q(t_ff_5_q[3]), .preset(demultiplexer_1_out1),
    .reset(demultiplexer_1_out0));  // open: Qn
  and and_2 (and_2_out, and_4_out, t_ff_5_q[2]);
  Demultiplexer #(.enable("false")) demultiplexer_1 (
    .out0(demultiplexer_1_out0), .out1(demultiplexer_1_out1), .in(or_1_out), .sel(slider_2_out[3]));
  xnor xnor_1 (xnor_1_out, t_ff_5_q[3], slider_1_out[3]);
  and and_3 (and_3_out, undriven_2, undriven);
  Demultiplexer #(.enable("false")) demultiplexer_2 (
    .out0(demultiplexer_2_out0), .out1(demultiplexer_2_out1), .in(or_2_out));  // open: sel
  or or_2 (or_2_out, undriven_3, undriven_4);
  and and_4 (and_4_out, and_5_out, t_ff_5_q[1]);
  Demultiplexer #(.enable("false")) demultiplexer_3 (
    .out0(demultiplexer_3_out0), .out1(demultiplexer_3_out1), .in(or_3_out), .sel(slider_2_out[2]));
  or or_3 (or_3_out, and_1_out, button_2_out);
  T_Flip_Flop t_ff_2 (
    .clk(undriven_5), .T(and_3_out), .Q(t_ff_2_q), .preset(demultiplexer_2_out1), .reset(demultiplexer_2_out0));  // open: Qn
  T_Flip_Flop t_ff_3 (
    .clk(button_1_out), .T(and_4_out), .Q(t_ff_5_q[2]), .preset(demultiplexer_3_out1),
    .reset(demultiplexer_3_out0));  // open: Qn
  xnor xnor_2 (xnor_2_out, t_ff_5_q[2], slider_1_out[2]);
  and and_5 (and_5_out, and_6_out, t_ff_5_q[0]);
  Demultiplexer #(.enable("false")) demultiplexer_4 (
    .out0(demultiplexer_4_out0), .out1(demultiplexer_4_out1), .in(or_4_out), .sel(slider_2_out[1]));
  or or_4 (or_4_out, and_1_out, button_2_out);
  T_Flip_Flop t_ff_4 (
    .clk(button_1_out), .T(and_5_out), .Q(t_ff_5_q[1]), .preset(demultiplexer_4_out1),
    .reset(demultiplexer_4_out0));  // open: Qn
  xnor xnor_3 (xnor_3_out, t_ff_5_q[1], slider_1_out[1]);
  and and_6 (and_6_out, 1'b1, 1'b1);
  Demultiplexer #(.enable("false")) demultiplexer_5 (
    .out0(demultiplexer_5_out0), .out1(demultiplexer_5_out1), .in(or_5_out), .sel(slider_2_out[0]));
  or or_5 (or_5_out, and_1_out, button_2_out);
  xnor xnor_4 (xnor_4_out, t_ff_5_q[0], slider_1_out[0]);
  T_Flip_Flop t_ff_5 (
    .clk(button_1_out), .T(and_6_out), .Q(t_ff_5_q[0]), .preset(demultiplexer_5_out1),
    .reset(demultiplexer_5_out0));  // open: Qn
  Slider #(.width(4), .value('hf)) slider_1 (.out(slider_1_out));
  Hex_Digit_Display hex_digit_display_1 (.value(t_ff_5_q));  // open: dp
  Button button_1 (.out(button_1_out));
  Button button_2 (.out(button_2_out));
  Slider #(.width(4)) slider_2 (.out(slider_2_out));

  // Notes on the sheet:
  //   ROOF
  //   FLOOR
  //   OUTPUT
  //   COUNT
  //   RESET
endmodule
