// Logisim project counter_sync.circ as structural Verilog: 1 circuit, main circuit main
module main (
);

  wire and_1_out, and_2_out, and_3_out, and_4_out, and_5_out, and_6_out, and_7_out, and_8_out, button_1_out,
       button_2_out, button_3_out, dipswitch_1_p1, dipswitch_1_p2, or_1_out, or_2_out, or_3_out, xnor_1_out,
       xnor_2_out, xnor_3_out, xnor_4_out;
  wire [3:0] j_k_ff_4_q, slider_1_out;

  and and_1 (and_1_out, ~j_k_ff_4_q[3], and_3_out);  // AND_Gate
  and and_2 (and_2_out, and_1_out, ~and_8_out);  // AND_Gate
  or or_1 (or_1_out, j_k_ff_4_q[3], and_8_out);
  J_K_Flip_Flop j_k_ff_1 (
    .J(and_2_out), .clk(button_1_out), .K(or_1_out), .Q(j_k_ff_4_q[3]), .reset(button_2_out));  // open: Qn, preset
  xnor xnor_1 (xnor_1_out, slider_1_out[3], j_k_ff_4_q[3]);
  and and_3 (and_3_out, ~j_k_ff_4_q[2], and_5_out);  // AND_Gate
  and and_4 (and_4_out, and_3_out, ~and_8_out);  // AND_Gate
  or or_2 (or_2_out, j_k_ff_4_q[2], and_8_out);
  xnor xnor_2 (xnor_2_out, slider_1_out[2], j_k_ff_4_q[2]);
  and and_5 (and_5_out, ~j_k_ff_4_q[1], j_k_ff_4_q[0]);  // AND_Gate
  J_K_Flip_Flop j_k_ff_2 (
    .J(and_4_out), .clk(button_1_out), .K(or_2_out), .Q(j_k_ff_4_q[2]), .reset(button_2_out));  // open: Qn, preset
  and and_6 (and_6_out, and_5_out, ~and_8_out);  // AND_Gate
  or or_3 (or_3_out, j_k_ff_4_q[1], and_8_out);
  J_K_Flip_Flop j_k_ff_3 (
    .J(and_6_out), .clk(button_1_out), .K(or_3_out), .Q(j_k_ff_4_q[1]), .reset(button_2_out));  // open: Qn, preset
  xnor xnor_3 (xnor_3_out, slider_1_out[1], j_k_ff_4_q[1]);
  and and_7 (and_7_out, 1'b1, ~and_8_out);  // AND_Gate
  Button button_1 (.out(button_1_out));
  J_K_Flip_Flop j_k_ff_4 (
    .J(and_7_out), .clk(button_1_out), .K(1'b1), .Q(j_k_ff_4_q[0]), .reset(button_2_out));  // open: Qn, preset
  Button button_2 (.out(button_2_out));
  xnor xnor_4 (xnor_4_out, slider_1_out[0], j_k_ff_4_q[0]);
  and and_8 (and_8_out, xnor_1_out, xnor_2_out, xnor_3_out, xnor_4_out);
  Hex_Digit_Display hex_digit_display_1 (.value(j_k_ff_4_q));  // open: dp
  Slider #(.width(4), .value('hf)) slider_1 (.out(slider_1_out));
  Hex_Digit_Display hex_digit_display_2 (.value(slider_1_out));  // open: dp
  Button button_3 (.out(button_3_out));
  // DipSwitch #(.NSwitches(2)) dipswitch_1: pin names not known; wires that end beside it: dipswitch_1_p1, dipswitch_1_p2
  J_K_Flip_Flop j_k_ff_5 (.J(dipswitch_1_p1), .clk(button_3_out), .K(dipswitch_1_p2));  // open: Q, Qn, preset, reset

  // Notes on the sheet:
  //   CONTADOR [0,X]
  //   CLOCK
  //   OUTPUT
  //   ASYNC RESET
  //   ROOF = X
endmodule
